// Logisim project ADDER_ANDGATES.circ as structural Verilog: 1 circuit, main circuit main
module main (
  input  in_1,
  input  in_2,
  input  A,
  input  B,
  input  C
);

  wire nand_1_out, nand_2_out, nand_3_out, nand_4_out, nand_5_out, nand_6_out, nand_7_out, nand_8_out,
       nand_9_out, nand_10_out, nand_11_out, nand_12_out, nand_13_out, nand_14_out;

  nand nand_1 (nand_1_out, A, B);
  nand nand_2 (nand_2_out, A, nand_1_out);
  nand nand_3 (nand_3_out, nand_1_out, B);
  nand nand_4 (nand_4_out, in_1, in_2);
  nand nand_5 (nand_5_out, nand_2_out, nand_3_out);
  nand nand_6 (nand_6_out, in_1, nand_4_out);
  nand nand_7 (nand_7_out, nand_4_out, in_2);
  nand nand_8 (nand_8_out, nand_5_out, C);
  nand nand_9 (nand_9_out, nand_5_out, nand_8_out);
  nand nand_10 (nand_10_out, nand_8_out, C);
  LED led_1 (.in(nand_11_out));
  nand nand_11 (nand_11_out, nand_6_out, nand_7_out);
  LED led_2 (.in(nand_12_out));
  nand nand_12 (nand_12_out, nand_4_out, nand_4_out);
  nand nand_13 (nand_13_out, nand_9_out, nand_10_out);
  nand nand_14 (nand_14_out, nand_8_out, nand_1_out);
  LED led_3 (.in(nand_13_out));
  LED led_4 (.in(nand_14_out));

  // Notes on the sheet:
  //   Half Adder
  //   Sum
  //   Carry
  //   SUM
  //   CARRY
endmodule
