// Logisim project adder_nor.circ as structural Verilog: 1 circuit, main circuit main
module main (
  input  x,
  input  y,
  input  z,
  output out_4,
  output out_5
);

  wire nor_1_out, nor_2_out, nor_3_out, nor_4_out, nor_5_out, nor_6_out, nor_7_out, nor_8_out, nor_9_out,
       nor_10_out, nor_11_out, nor_12_out;

  not nor_1 (nor_1_out, x);  // NOR_Gate
  not nor_2 (nor_2_out, y);  // NOR_Gate
  not nor_3 (nor_3_out, z);  // NOR_Gate
  nor nor_4 (nor_4_out, nor_1_out, y, z);
  nor nor_5 (nor_5_out, x, nor_2_out, z);
  nor nor_6 (nor_6_out, nor_3_out, y, x);
  nor nor_7 (nor_7_out, nor_3_out, nor_2_out, nor_1_out);
  nor nor_8 (nor_8_out, nor_1_out, nor_2_out);
  nor nor_9 (nor_9_out, nor_1_out, nor_3_out);
  nor nor_10 (nor_10_out, nor_3_out, nor_2_out);
  nor nor_11 (nor_11_out, nor_8_out, nor_9_out, nor_10_out);
  nor nor_12 (nor_12_out, nor_4_out, nor_5_out, nor_6_out, nor_7_out);
  nor nor_13 (out_5, nor_11_out, nor_11_out);
  nor nor_14 (out_4, nor_12_out, nor_12_out);

  // Notes on the sheet:
  //   S
  //   C
endmodule
