// Logisim project subtractor_nand.circ as structural Verilog: 1 circuit, main circuit main
module main (
  input  x,
  input  y,
  input  z,
  output D,
  output out_5
);

  wire nand_1_out, nand_2_out, nand_3_out, nand_4_out, nand_5_out, nand_6_out, nand_7_out, nand_8_out,
       nand_9_out, nand_10_out;

  not nand_1 (nand_1_out, x);  // NAND_Gate
  nand nand_2 (nand_2_out, nand_1_out, y);
  nand nand_3 (nand_3_out, nand_1_out, z);
  nand nand_4 (nand_4_out, y, z);
  not nand_5 (nand_5_out, y);  // NAND_Gate
  not nand_6 (nand_6_out, z);  // NAND_Gate
  nand nand_7 (nand_7_out, z, nand_5_out, nand_1_out);
  nand nand_8 (nand_8_out, nand_1_out, nand_6_out, y);
  nand nand_9 (nand_9_out, x, nand_5_out, nand_6_out);
  nand nand_10 (nand_10_out, z, x, y);
  nand nand_11 (out_5, nand_2_out, nand_3_out, nand_4_out);
  nand nand_12 (D, nand_9_out, nand_10_out, nand_8_out, nand_7_out);

  // Notes on the sheet:
  //   B
endmodule
