// Logisim project bus3statebuffer.circ as structural Verilog: 1 circuit, main circuit main
module main (
  input  [1:0] in_1,
  input  [1:0] in_2
);

  wire clock_1_out, decoder_1_out0, decoder_1_out1, decoder_1_out2, decoder_1_out3, decoder_2_out0,
       decoder_2_out1, decoder_2_out2, decoder_2_out3;
  wire [3:0] controlled_buffer_1_out, register_1_q, register_2_q, register_3_q, register_4_q;

  Decoder #(.select(2)) decoder_1 (
    .out0(decoder_1_out0), .out1(decoder_1_out1), .out2(decoder_1_out2), .out3(decoder_1_out3), .sel(in_2));  // open: en
  Clock clock_1 (.out(clock_1_out));
  Register #(.width(4)) register_1 (
    .D(controlled_buffer_1_out), .en(decoder_1_out0), .Q(register_1_q), .clk(clock_1_out));  // open: clr
  Register #(.width(4)) register_2 (
    .D(controlled_buffer_1_out), .en(decoder_1_out1), .Q(register_2_q), .clk(clock_1_out));  // open: clr
  Register #(.width(4)) register_3 (
    .D(controlled_buffer_1_out), .en(decoder_1_out2), .Q(register_3_q), .clk(clock_1_out));  // open: clr
  Register #(.width(4)) register_4 (
    .D(controlled_buffer_1_out), .en(decoder_1_out3), .Q(register_4_q), .clk(clock_1_out));  // open: clr
  Decoder #(.select(2)) decoder_2 (
    .out0(decoder_2_out0), .out1(decoder_2_out1), .out2(decoder_2_out2), .out3(decoder_2_out3), .sel(in_1));  // open: en
  assign controlled_buffer_1_out[0] = decoder_2_out0 ? register_1_q[0] : 1'bz;  // Controlled_Buffer controlled_buffer_1
  assign controlled_buffer_1_out[0] = decoder_2_out1 ? register_2_q[0] : 1'bz;  // Controlled_Buffer controlled_buffer_2
  assign controlled_buffer_1_out[0] = decoder_2_out2 ? register_3_q[0] : 1'bz;  // Controlled_Buffer controlled_buffer_3
  assign controlled_buffer_1_out[0] = decoder_2_out3 ? register_4_q[0] : 1'bz;  // Controlled_Buffer controlled_buffer_4
  assign controlled_buffer_1_out[1] = decoder_2_out0 ? register_1_q[1] : 1'bz;  // Controlled_Buffer controlled_buffer_5
  assign controlled_buffer_1_out[1] = decoder_2_out1 ? register_2_q[1] : 1'bz;  // Controlled_Buffer controlled_buffer_6
  assign controlled_buffer_1_out[1] = decoder_2_out2 ? register_3_q[1] : 1'bz;  // Controlled_Buffer controlled_buffer_7
  assign controlled_buffer_1_out[1] = decoder_2_out3 ? register_4_q[1] : 1'bz;  // Controlled_Buffer controlled_buffer_8
  assign controlled_buffer_1_out[2] = decoder_2_out0 ? register_1_q[2] : 1'bz;  // Controlled_Buffer controlled_buffer_9
  assign controlled_buffer_1_out[2] = decoder_2_out1 ? register_2_q[2] : 1'bz;  // Controlled_Buffer controlled_buffer_10
  assign controlled_buffer_1_out[2] = decoder_2_out2 ? register_3_q[2] : 1'bz;  // Controlled_Buffer controlled_buffer_11
  assign controlled_buffer_1_out[2] = decoder_2_out3 ? register_4_q[2] : 1'bz;  // Controlled_Buffer controlled_buffer_12
  assign controlled_buffer_1_out[3] = decoder_2_out0 ? register_1_q[3] : 1'bz;  // Controlled_Buffer controlled_buffer_13
  assign controlled_buffer_1_out[3] = decoder_2_out1 ? register_2_q[3] : 1'bz;  // Controlled_Buffer controlled_buffer_14
  assign controlled_buffer_1_out[3] = decoder_2_out2 ? register_3_q[3] : 1'bz;  // Controlled_Buffer controlled_buffer_15
  assign controlled_buffer_1_out[3] = decoder_2_out3 ? register_4_q[3] : 1'bz;  // Controlled_Buffer controlled_buffer_16
endmodule
