// Logisim project busmultiplexer.circ as structural Verilog: 1 circuit, main circuit main
module main (
  input  [1:0] in_1,
  input  [1:0] in_2
);

  wire clock_1_out, decoder_1_out0, decoder_1_out1, decoder_1_out2, decoder_1_out3;
  wire [3:0] multiplexer_1_out, register_1_q, register_2_q, register_3_q, register_4_q;

  Multiplexer #(.select(2)) multiplexer_1 (
    .in0(register_1_q[0]), .in1(register_2_q[0]), .in2(register_3_q[0]), .in3(register_4_q[0]),
    .out(multiplexer_1_out[0]), .sel(in_1));  // open: en
  Register #(.width(4)) register_1 (
    .D(multiplexer_1_out), .en(decoder_1_out0), .Q(register_1_q), .clk(clock_1_out));  // open: clr
  Multiplexer #(.select(2)) multiplexer_2 (
    .in0(register_1_q[1]), .in1(register_2_q[1]), .in2(register_3_q[3]), .in3(register_3_q[3]),
    .out(multiplexer_1_out[1]), .sel(in_1));  // open: en
  Register #(.width(4)) register_2 (
    .D(multiplexer_1_out), .en(decoder_1_out1), .Q(register_2_q), .clk(clock_1_out));  // open: clr
  Decoder #(.select(2)) decoder_1 (
    .out0(decoder_1_out0), .out1(decoder_1_out1), .out2(decoder_1_out2), .out3(decoder_1_out3), .sel(in_2));  // open: en
  Multiplexer #(.select(2)) multiplexer_3 (
    .in0(register_1_q[2]), .in1(register_2_q[2]), .in2(register_3_q[2]), .in3(register_4_q[3]),
    .out(multiplexer_1_out[2]), .sel(in_1));  // open: en
  Register #(.width(4)) register_3 (
    .D(multiplexer_1_out), .en(decoder_1_out2), .Q({register_3_q[3:2], register_3_q[3], register_3_q[0]}),
    .clk(clock_1_out));  // open: clr
  Register #(.width(4)) register_4 (
    .D(multiplexer_1_out), .en(decoder_1_out3), .Q({{2{register_4_q[3]}}, register_3_q[3], register_4_q[0]}),
    .clk(clock_1_out));  // open: clr
  Multiplexer #(.select(2)) multiplexer_4 (
    .in0(register_1_q[3]), .in1(register_2_q[3]), .in2(register_3_q[3]), .in3(register_4_q[3]),
    .out(multiplexer_1_out[3]), .sel(in_1));  // open: en
  Clock clock_1 (.out(clock_1_out));
endmodule
