// Logisim project alSu.circ as structural Verilog: 1 circuit, main circuit main
module main (
  input  A0,
  input  A2,
  input  A4,
  input  A8,
  input  Cin,
  input  B1,
  input  in_7,
  input  B2,
  input  in_9,
  input  B4,
  input  in_11,
  input  [1:0] in_12,
  input  B8,
  input  in_14,
  input  [1:0] _00___Add,
  input  IL,
  input  in_17,
  input  in_18,
  output [3:0] out_19,
  output [3:0] out_20
);

  wire adder_1_cout, adder_2_cout, adder_3_cout, multiplexer_1_out, multiplexer_2_out, multiplexer_3_out,
       multiplexer_4_out, not_1_out, not_2_out, not_4_out, not_6_out, not_8_out, xor_1_out, xor_2_out;
  wire [3:0] adder_1_out, and_1_out, not_9_out, or_1_out, xor_3_out;

  not not_1 (not_1_out, B1);
  Multiplexer #(.select(2)) multiplexer_1 (
    .in0(B1), .in1(not_1_out), .in2(in_7), .in3(not_2_out), .out(multiplexer_1_out), .sel(_00___Add));  // open: en
  not not_2 (not_2_out, in_7);
  // NOT_Gate not_3 has open pins: in=B2, out=open
  Multiplexer #(.select(2)) multiplexer_2 (
    .in0(B2), .in2(in_9), .in3(not_4_out), .out(multiplexer_2_out), .sel(_00___Add));  // open: in1, en
  not not_4 (not_4_out, in_9);
  // NOT_Gate not_5 has open pins: in=B4, out=open
  Multiplexer #(.select(2)) multiplexer_3 (
    .in0(B4), .in2(in_11), .in3(not_6_out), .out(multiplexer_3_out), .sel(_00___Add));  // open: in1, en
  not not_6 (not_6_out, in_11);
  // NOT_Gate not_7 has open pins: in=B8, out=open
  Multiplexer #(.select(2)) multiplexer_4 (
    .in0(B8), .in2(in_14), .in3(not_8_out), .out(multiplexer_4_out), .sel(_00___Add));  // open: in1, en
  not not_8 (not_8_out, in_14);
  Adder #(.width(1)) adder_1 (.a(A0), .b(multiplexer_1_out), .out(adder_1_out[0]), .cin(Cin), .cout(adder_1_cout));
  Adder #(.width(1)) adder_2 (
    .a(A2), .b(multiplexer_2_out), .out(adder_1_out[1]), .cin(adder_1_cout), .cout(adder_2_cout));
  Adder #(.width(1)) adder_3 (
    .a(A4), .b(multiplexer_3_out), .out(adder_1_out[2]), .cin(adder_2_cout), .cout(adder_3_cout));
  Adder #(.width(1)) adder_4 (.a(A8), .b(multiplexer_4_out), .out(adder_1_out[3]), .cin(adder_3_cout));  // open: cout
  xor xor_1 (xor_1_out, A8, A4);
  Multiplexer #(.select(2)) multiplexer_5 (.in0(in_17), .in1(A0), .in2(A8));  // open: in3, out, sel, en
  xor xor_2 (xor_2_out, xor_1_out, A4);
  Multiplexer multiplexer_6 (.in0(A0), .in1(IL), .out(out_20[0]), .sel(in_18));  // open: en
  Multiplexer multiplexer_7 (.in0(A2), .out(out_20[1]), .sel(in_18));  // open: in1, en
  Multiplexer multiplexer_8 (.in0(A4), .out(out_20[2]), .sel(in_18));  // open: in1, en
  Multiplexer multiplexer_9 (.in0(A8), .in1(xor_2_out), .out(out_20[3]), .sel(in_18));  // open: en
  assign and_1_out = {B8, B4, B2, B1} & {A8, A4, A2, A0};  // AND_Gate and_1, 4 bits wide
  assign or_1_out = {B8, B4, B2, B1} | {A8, A4, A2, A0};  // OR_Gate or_1, 4 bits wide
  assign xor_3_out = {B8, B4, B2, B1} ^ {A8, A4, A2, A0};  // XOR_Gate xor_3, 4 bits wide
  assign not_9_out = ~{A8, A4, A2, A0};  // NOT_Gate not_9, 4 bits wide
  Multiplexer #(.select(2), .width(4)) multiplexer_10 (
    .in0(and_1_out), .in1(or_1_out), .in2(xor_3_out), .in3(not_9_out), .out(out_19), .sel(in_12));  // open: en

  // Notes on the sheet:
  //   01:Subtract
  //   L/R
endmodule
