// Logisim project basic computer fetch.circ as structural Verilog: 1 circuit, main circuit main
module main (
  input  [3:0] in_1,
  input  in_2,
  input  [3:0] in_3
);

  wire clock_1_out, decoder_1_out0;
  wire [2:0] counter_1_q;
  wire [2:2] decoder_1_out1;
  wire [7:0] register_7_q;
  wire [11:0] counter_2_q, register_1_q;
  wire [15:0] multiplexer_1_out, ram_1_data, register_2_q, register_3_q, register_5_q, register_6_q;

  Decoder #(.select(3)) decoder_1 (
    .out0(decoder_1_out0), .out1(decoder_1_out1[2]), .sel(counter_1_q));  // open: out2, out3, out4, out5, out6, out7, en
  Counter #(.width(3), .max('h7)) counter_1 (.Q(counter_1_q), .clk(clock_1_out));  // open: load, D, count, carry, clr
  Register #(.width(12)) register_1 (
    .D(multiplexer_1_out[11:0]), .en(decoder_1_out0), .Q(register_1_q), .clk(clock_1_out));  // open: clr
  Counter #(.width(12), .max('hfff)) counter_2 (
    .D(multiplexer_1_out[11:0]), .count(decoder_1_out1[2]), .Q(counter_2_q), .clk(clock_1_out));  // open: load, carry, clr
  Register #(.width(16)) register_2 (.D(multiplexer_1_out), .Q(register_2_q), .clk(clock_1_out));  // open: en, clr
  Register #(.width(16)) register_3 (.Q(register_3_q), .clk(clock_1_out));  // open: D, en, clr
  Register register_4 (.clk(clock_1_out));  // open: D, en, Q, clr
  Register #(.width(16)) register_5 (
    .D(multiplexer_1_out), .en(decoder_1_out1[2]), .Q(register_5_q), .clk(clock_1_out));  // open: clr
  Register #(.width(16)) register_6 (.D(multiplexer_1_out), .Q(register_6_q), .clk(clock_1_out));  // open: en, clr
  Register register_7 (.D(multiplexer_1_out[7:0]), .Q(register_7_q), .clk(clock_1_out));  // open: en, clr
  RAM #(.addrWidth(12), .dataWidth(16), .bus("separate")) ram_1 (
    .addr(register_1_q), .din(multiplexer_1_out), .data(ram_1_data), .clk(clock_1_out));  // open: str, sel, ld, clr
  Clock clock_1 (.out(clock_1_out));
  Multiplexer #(.select(3), .width(16)) multiplexer_1 (
    .in1({in_1, register_1_q}), .in2({in_3, counter_2_q}), .in3(register_2_q), .in4(register_3_q),
    .in5(register_5_q), .in6(register_6_q), .in7(ram_1_data), .out(multiplexer_1_out),
    .sel({decoder_1_out1[2], in_2, decoder_1_out1[2]}));  // open: in0, en

  // Notes on the sheet:
  //   AR
  //   DR
  //   AC
  //   INPR
  //   IR
  //   MEM
  //   TR
endmodule
